// Logisim project cpu.circ as structural Verilog: 14 circuits, main circuit main
module main (
  input  reset_key,
  input  g_reg_reset,
  input  reset_tty,
  input  PC_reset
);

  wire ble_PC_plus1B, bne_PC_plus1B, keyboard_1_avail, main_clk, memory_latch_1_oe_latched,
       memory_latch_1_we_latched, not_1_out, not_3_out, read_key, WE_Memory, write_tty;
  wire [2:0] multiplexer_2_out;
  wire [6:0] bit_extender_3_out;
  wire [7:0] key_in_val;
  wire [11:0] address;
  wire [15:0] alu_out, immediate_16, j_imm_16, memory_latch_1_address_latched,
       memory_latch_1_data_in_latched, multiplexer_1_out, multiplexer_3_out, multiplexer_4_out,
       multiplexer_5_out, multiplexer_6_out, PC_plus_1_B, PC_plus_one, PC_reg_out, ram_out, read_a_value,
       read_b_value;
  wire [15:12] instruction;

  Clock clk (.out(main_clk));
  not not_1 (not_1_out, main_clk);
  // Probe on {instruction, address}
  single_reg PC (.data_in(multiplexer_1_out), .clk(not_1_out), .WE(1'b1), .reset(PC_reset), .reg_out(PC_reg_out));
  // Probe on PC_reg_out
  ROM #(.addrWidth(16), .dataWidth(16)) rom_1 (.addr(PC_reg_out), .data({instruction, address}));
  // Probe on instruction
  Multiplexer #(.select(4), .width(16), .enable("false")) multiplexer_1 (
    .in0(PC_plus_one), .in1(PC_plus_one), .in2(PC_plus_one), .in3(PC_plus_one), .in4(PC_plus_one),
    .in5(PC_plus_one), .in6(PC_plus_one), .in7(PC_plus_one), .in8(PC_plus_one), .in9(multiplexer_3_out),
    .in10(multiplexer_4_out), .in11(j_imm_16), .in12(read_a_value), .in13(j_imm_16), .in14(PC_plus_one),
    .in15(PC_plus_one), .out(multiplexer_1_out), .sel(instruction));
  // Probe on instruction
  Multiplexer #(.select(4), .width(3), .enable("false")) multiplexer_2 (
    .in0(address[5:3]), .in1(address[8:6]), .in2(address[5:3]), .in3(address[5:3]), .in4(address[5:3]),
    .in5(address[5:3]), .in6(address[5:3]), .in7(address[8:6]), .in8(3'b000), .in9(3'b000), .in10(3'b000),
    .in11(3'b000), .in12(3'b000), .in13(3'b111), .in14(address[8:6]), .in15(3'b000), .out(multiplexer_2_out),
    .sel(instruction));
  assign j_imm_16 = {{4{address[11]}}, address};  // Bit_Extender bit_extender_1
  // Probe on address
  // Probe on address[5:0]
  // Probe on address[2:0]
  // Probe on address[5:3]
  // Probe on address[8:6]
  // Probe on address[11:9]
  // Probe on multiplexer_4_out
  Multiplexer #(.width(16), .enable("false")) multiplexer_3 (
    .in0(PC_plus_one), .in1(PC_plus_1_B), .out(multiplexer_3_out), .sel(bne_PC_plus1B));
  Multiplexer #(.width(16), .enable("false")) multiplexer_4 (
    .in0(PC_plus_one), .in1(PC_plus_1_B), .out(multiplexer_4_out), .sel(ble_PC_plus1B));
  // Probe on PC_plus_one
  // Probe on PC_plus_1_B
  sixteen_adder sixteen_adder_1 (.a_in(16'h1), .b_in(PC_reg_out), .sum(PC_plus_one));  // open: sub, c_out
  // Probe on multiplexer_2_out
  // Probe on PC_plus_one
  // Probe on multiplexer_6_out
  assign immediate_16 = {{10{address[5]}}, address[5:0]};  // Bit_Extender bit_extender_2
  RegisterFile registerfile_1 (
    .data_in(multiplexer_6_out), .write_enable(1'b1), .write_register(multiplexer_2_out),
    .global_reset(g_reg_reset), .read_A(address[11:9]), .read_B(address[8:6]), .clk_reg(main_clk),
    .read_a_val(read_a_value), .read_b_val(read_b_value));
  Keyboard #(.trigger("falling")) keyboard_1 (
    .clk(main_clk), .re(read_key), .clr(reset_key), .avail(keyboard_1_avail), .data(key_in_val[6:0]));
  Multiplexer #(.select(4), .width(16), .enable("false")) multiplexer_5 (
    .in0(read_b_value), .in1(immediate_16), .in2(read_b_value), .in3({16{1'b0}}), .in4({16{1'b0}}),
    .in5(read_b_value), .in6({16{1'b0}}), .in7(immediate_16), .in8(immediate_16), .in9(read_b_value),
    .in10(read_b_value), .in11({16{1'b0}}), .in12({16{1'b0}}), .in13(PC_plus_one),
    .in14({{8{1'b0}}, key_in_val}), .in15(immediate_16), .out(multiplexer_5_out), .sel(instruction));
  // Probe on read_a_value
  // Probe on multiplexer_5_out
  // Probe on key_in_val[6:0]
  not not_2 (key_in_val[7], keyboard_1_avail);
  sixteen_adder sixteen_adder_2 (.a_in(PC_plus_one), .b_in(immediate_16), .sum(PC_plus_1_B));  // open: sub, c_out
  Multiplexer #(.select(4), .width(16), .enable("false")) multiplexer_6 (
    .in0(alu_out), .in1(alu_out), .in2(alu_out), .in3(alu_out), .in4(alu_out), .in5(alu_out), .in6(alu_out),
    .in7(ram_out), .in13(alu_out), .in14(alu_out), .out(multiplexer_6_out), .sel(instruction));  // open: in8, in9, in10, in11, in12, in15
  ALU alu_1 (
    .in1_val(read_a_value), .in2_val(multiplexer_5_out), .OpType(instruction), .shamt_in(address[2:0]),
    .out_val(alu_out), .bne(bne_PC_plus1B), .ble(ble_PC_plus1B));  // open: ovf
  Bit_Extender #(.in_width(16), .out_width(7)) bit_extender_3 (.in(read_a_value), .out(bit_extender_3_out));
  // Probe on alu_out
  TTY #(.rows(13), .cols(80)) tty_1 (.data(bit_extender_3_out), .clk(main_clk), .we(write_tty), .clr(reset_tty));
  Decoder #(.select(4), .enable("false")) decoder_1 (
    .out8(WE_Memory), .out14(read_key), .out15(write_tty), .sel(instruction));  // open: out0, out1, out2, out3, out4, out5, out6, out7, out9, out10, out11, out12, out13
  not not_3 (not_3_out, main_clk);
  // Probe on read_b_value
  memory_latch memory_latch_1 (
    .address(alu_out), .WE(WE_Memory), .clk(not_3_out), .data_in(read_b_value),
    .address_latched(memory_latch_1_address_latched), .WE_latched(memory_latch_1_we_latched),
    .OE_latched(memory_latch_1_oe_latched), .data_in_latched(memory_latch_1_data_in_latched));
  // Probe on memory_latch_1_address_latched
  // Probe on memory_latch_1_data_in_latched
  RAM #(.addrWidth(16), .dataWidth(16), .trigger("high"), .databus("bibus")) ram_1 (
    .addr(memory_latch_1_address_latched), .we(memory_latch_1_we_latched), .oe(memory_latch_1_oe_latched),
    .din(memory_latch_1_data_in_latched), .dout(ram_out));

  // Other names for the same wires on the sheet: immediate[5:0] = address[5:0]; instruction[11:0] = address;
  //   j_imm[11:0] = address; shamt[2:0] = address[2:0]; Rd[2:0] = address[5:3]; Rt[2:0] = address[8:6];
  //   Rs[2:0] = address[11:9]; opcode[3:0] = instruction
endmodule

module memory_latch (
  input  [15:0] address,
  input  WE,
  input  clk,
  input  [15:0] data_in,
  output [15:0] address_latched,
  output WE_latched,
  output OE_latched,
  output [15:0] data_in_latched
);

  wire DMwe_latch_q;
  wire [15:0] addr_latch_q;

  Register #(.width(16), .trigger("falling")) addr_latch (
    .D(address), .en(WE), .clk(clk), .Q(addr_latch_q));  // open: clr
  D_Flip_Flop #(.trigger("falling")) DMwe_latch (.D(WE), .clk(clk), .Q(DMwe_latch_q));  // open: Qn, preset, reset
  Register #(.width(16), .trigger("falling")) data_to_be_written (
    .D(data_in), .en(WE), .clk(clk), .Q(data_in_latched));  // open: clr
  Multiplexer #(.width(16), .enable("false")) multiplexer_1 (
    .in0(address), .in1(addr_latch_q), .out(address_latched), .sel(DMwe_latch_q));
  and and_1 (WE_latched, clk, DMwe_latch_q);
  not not_1 (OE_latched, WE_latched);
endmodule

module single_reg (
  input  [15:0] data_in,
  input  clk,
  input  WE,
  input  reset,
  output [15:0] reg_out
);

  wire clk_WE;

  and and_1 (clk_WE, clk, WE);
  D_Flip_Flop d_ff_1 (.D(data_in[0]), .clk(clk_WE), .Q(reg_out[0]), .reset(reset));  // open: Qn, preset
  D_Flip_Flop d_ff_2 (.D(data_in[1]), .clk(clk_WE), .Q(reg_out[1]), .reset(reset));  // open: Qn, preset
  D_Flip_Flop d_ff_3 (.D(data_in[2]), .clk(clk_WE), .Q(reg_out[2]), .reset(reset));  // open: Qn, preset
  D_Flip_Flop d_ff_4 (.D(data_in[3]), .clk(clk_WE), .Q(reg_out[3]), .reset(reset));  // open: Qn, preset
  D_Flip_Flop d_ff_5 (.D(data_in[4]), .clk(clk_WE), .Q(reg_out[4]), .reset(reset));  // open: Qn, preset
  D_Flip_Flop d_ff_6 (.D(data_in[5]), .clk(clk_WE), .Q(reg_out[5]), .reset(reset));  // open: Qn, preset
  D_Flip_Flop d_ff_7 (.D(data_in[6]), .clk(clk_WE), .Q(reg_out[6]), .reset(reset));  // open: Qn, preset
  D_Flip_Flop d_ff_8 (.D(data_in[7]), .clk(clk_WE), .Q(reg_out[7]), .reset(reset));  // open: Qn, preset
  D_Flip_Flop d_ff_9 (.D(data_in[8]), .clk(clk_WE), .Q(reg_out[8]), .reset(reset));  // open: Qn, preset
  D_Flip_Flop d_ff_10 (.D(data_in[9]), .clk(clk_WE), .Q(reg_out[9]), .reset(reset));  // open: Qn, preset
  D_Flip_Flop d_ff_11 (.D(data_in[10]), .clk(clk_WE), .Q(reg_out[10]), .reset(reset));  // open: Qn, preset
  D_Flip_Flop d_ff_12 (.D(data_in[11]), .clk(clk_WE), .Q(reg_out[11]), .reset(reset));  // open: Qn, preset
  D_Flip_Flop d_ff_13 (.D(data_in[12]), .clk(clk_WE), .Q(reg_out[12]), .reset(reset));  // open: Qn, preset
  D_Flip_Flop d_ff_14 (.D(data_in[13]), .clk(clk_WE), .Q(reg_out[13]), .reset(reset));  // open: Qn, preset
  D_Flip_Flop d_ff_15 (.D(data_in[14]), .clk(clk_WE), .Q(reg_out[14]), .reset(reset));  // open: Qn, preset
  D_Flip_Flop d_ff_16 (.D(data_in[15]), .clk(clk_WE), .Q(reg_out[15]), .reset(reset));  // open: Qn, preset
endmodule

module RegisterFile (
  input  [15:0] data_in,
  input  write_enable,
  input  [2:0] write_register,
  input  global_reset,
  input  [2:0] read_A,
  input  [2:0] read_B,
  input  clk_reg,
  output [15:0] read_a_val,
  output [15:0] read_b_val
);

  wire r0, r1, r2, r3, r4, r5, r6, r7, tr0a, tr0b, tr1a, tr1b, tr2a, tr2b, tr3a, tr3b, tr4a, tr4b, tr5a,
       tr5b, tr6a, tr6b, tr7a, tr7b;
  wire [15:0] reg0_reg_out, reg1_reg_out, reg2_reg_out, reg3_reg_out, reg4_reg_out, reg5_reg_out,
       reg6_reg_out, reg7_reg_out;

  Decoder #(.select(3)) decoder_1 (
    .out0(r0), .out1(r1), .out2(r2), .out3(r3), .out4(r4), .out5(r5), .out6(r6), .out7(r7),
    .sel(write_register), .en(write_enable));
  Decoder #(.select(3), .enable("false")) decoder_2 (
    .out0(tr0a), .out1(tr1a), .out2(tr2a), .out3(tr3a), .out4(tr4a), .out5(tr5a), .out6(tr6a), .out7(tr7a),
    .sel(read_A));
  Decoder #(.select(3), .enable("false")) decoder_3 (
    .out0(tr0b), .out1(tr1b), .out2(tr2b), .out3(tr3b), .out4(tr4b), .out5(tr5b), .out6(tr6b), .out7(tr7b),
    .sel(read_B));
  single_reg reg0 (.data_in({16{1'b0}}), .clk(clk_reg), .WE(r0), .reset(global_reset), .reg_out(reg0_reg_out));
  single_reg reg1 (.data_in(data_in), .clk(clk_reg), .WE(r1), .reset(global_reset), .reg_out(reg1_reg_out));
  single_reg reg2 (.data_in(data_in), .clk(clk_reg), .WE(r2), .reset(global_reset), .reg_out(reg2_reg_out));
  single_reg reg3 (.data_in(data_in), .clk(clk_reg), .WE(r3), .reset(global_reset), .reg_out(reg3_reg_out));
  single_reg reg4 (.data_in(data_in), .clk(clk_reg), .WE(r4), .reset(global_reset), .reg_out(reg4_reg_out));
  single_reg reg5 (.data_in(data_in), .clk(clk_reg), .WE(r5), .reset(global_reset), .reg_out(reg5_reg_out));
  single_reg reg6 (.data_in(data_in), .clk(clk_reg), .WE(r6), .reset(global_reset), .reg_out(reg6_reg_out));
  single_reg reg7 (.data_in(data_in), .clk(clk_reg), .WE(r7), .reset(global_reset), .reg_out(reg7_reg_out));
  // Probe on reg0_reg_out
  // Probe on reg1_reg_out
  // Probe on reg2_reg_out
  // Probe on reg3_reg_out
  // Probe on reg4_reg_out
  // Probe on reg5_reg_out
  // Probe on reg6_reg_out
  // Probe on reg7_reg_out
  assign read_a_val = tr0a ? reg0_reg_out : 16'bz;  // Controlled_Buffer controlled_buffer_1
  assign read_a_val = tr1a ? reg1_reg_out : 16'bz;  // Controlled_Buffer controlled_buffer_2
  assign read_a_val = tr2a ? reg2_reg_out : 16'bz;  // Controlled_Buffer controlled_buffer_3
  assign read_a_val = tr3a ? reg3_reg_out : 16'bz;  // Controlled_Buffer controlled_buffer_4
  assign read_a_val = tr4a ? reg4_reg_out : 16'bz;  // Controlled_Buffer controlled_buffer_5
  assign read_a_val = tr5a ? reg5_reg_out : 16'bz;  // Controlled_Buffer controlled_buffer_6
  assign read_a_val = tr6a ? reg6_reg_out : 16'bz;  // Controlled_Buffer controlled_buffer_7
  assign read_a_val = tr7a ? reg7_reg_out : 16'bz;  // Controlled_Buffer controlled_buffer_8
  assign read_b_val = tr0b ? reg0_reg_out : 16'bz;  // Controlled_Buffer controlled_buffer_9
  assign read_b_val = tr1b ? reg1_reg_out : 16'bz;  // Controlled_Buffer controlled_buffer_10
  assign read_b_val = tr2b ? reg2_reg_out : 16'bz;  // Controlled_Buffer controlled_buffer_11
  assign read_b_val = tr3b ? reg3_reg_out : 16'bz;  // Controlled_Buffer controlled_buffer_12
  assign read_b_val = tr4b ? reg4_reg_out : 16'bz;  // Controlled_Buffer controlled_buffer_13
  assign read_b_val = tr5b ? reg5_reg_out : 16'bz;  // Controlled_Buffer controlled_buffer_14
  assign read_b_val = tr6b ? reg6_reg_out : 16'bz;  // Controlled_Buffer controlled_buffer_15
  assign read_b_val = tr7b ? reg7_reg_out : 16'bz;  // Controlled_Buffer controlled_buffer_16

  // Other names for the same wires on the sheet: data_in_reg[15:0] = data_in; g_reset = global_reset
endmodule

module tty_keyboard (
  input  read,
  input  reset,
  input  clear
);

  wire clock_1_out, keyboard_1_avail;
  wire [6:0] keyboard_1_data;

  Clock clock_1 (.out(clock_1_out));
  Keyboard #(.trigger("falling")) keyboard_1 (
    .clk(clock_1_out), .re(read), .clr(reset), .avail(keyboard_1_avail), .data(keyboard_1_data));
  TTY #(.rows(13), .cols(80), .trigger("falling")) tty_1 (
    .data(keyboard_1_data), .clk(clock_1_out), .we(keyboard_1_avail), .clr(clear));
  // Probe on keyboard_1_data
  // Probe on keyboard_1_avail
endmodule

module fetch (
  input  clk_pc,
  input  reset_PC,
  output [15:0] instruction
);

  wire not_1_out;
  wire [15:0] PC_reg_out, sixteen_adder_1_sum;

  not not_1 (not_1_out, clk_pc);
  single_reg PC (.data_in(sixteen_adder_1_sum), .clk(not_1_out), .WE(1'b1), .reset(reset_PC), .reg_out(PC_reg_out));
  // Probe on PC_reg_out
  ROM #(.addrWidth(16), .dataWidth(16)) rom_1 (.addr(PC_reg_out), .data(instruction));
  sixteen_adder sixteen_adder_1 (.a_in(16'h1), .b_in(PC_reg_out), .sum(sixteen_adder_1_sum));  // open: sub, c_out
  // Probe on sixteen_adder_1_sum
endmodule

module full_adder (
  input  a_in,
  input  b_in,
  input  c_in,
  output sum,
  output c_out
);

  wire and_1_out, and_2_out, xor_1_out;

  and and_1 (and_1_out, b_in, a_in);
  xor xor_1 (xor_1_out, a_in, b_in);
  and and_2 (and_2_out, xor_1_out, c_in);
  xor xor_2 (sum, xor_1_out, c_in);
  or or_1 (c_out, and_2_out, and_1_out);
endmodule

module sixteen_adder (
  input  [15:0] a_in,
  input  sub,
  input  [15:0] b_in,
  output [15:0] sum,
  output c_out
);

  wire full_adder_1_c_out, full_adder_2_c_out, full_adder_3_c_out, full_adder_4_c_out, full_adder_5_c_out,
       full_adder_6_c_out, full_adder_7_c_out, full_adder_8_c_out, full_adder_9_c_out, full_adder_10_c_out,
       full_adder_11_c_out, full_adder_12_c_out, full_adder_13_c_out, full_adder_14_c_out,
       full_adder_15_c_out, full_adder_16_c_out, xor_1_out, xor_2_out, xor_3_out, xor_4_out, xor_5_out,
       xor_6_out, xor_7_out, xor_8_out, xor_9_out, xor_10_out, xor_11_out, xor_12_out, xor_13_out,
       xor_14_out, xor_15_out, xor_16_out;

  xor xor_1 (xor_1_out, sub, b_in[0]);
  full_adder full_adder_1 (.a_in(a_in[0]), .b_in(xor_1_out), .c_in(sub), .sum(sum[0]), .c_out(full_adder_1_c_out));
  xor xor_2 (xor_2_out, sub, b_in[1]);
  full_adder full_adder_2 (
    .a_in(a_in[1]), .b_in(xor_2_out), .c_in(full_adder_1_c_out), .sum(sum[1]), .c_out(full_adder_2_c_out));
  xor xor_3 (xor_3_out, sub, b_in[2]);
  full_adder full_adder_3 (
    .a_in(a_in[2]), .b_in(xor_3_out), .c_in(full_adder_2_c_out), .sum(sum[2]), .c_out(full_adder_3_c_out));
  xor xor_4 (xor_4_out, sub, b_in[3]);
  full_adder full_adder_4 (
    .a_in(a_in[3]), .b_in(xor_4_out), .c_in(full_adder_3_c_out), .sum(sum[3]), .c_out(full_adder_4_c_out));
  xor xor_5 (xor_5_out, sub, b_in[4]);
  full_adder full_adder_5 (
    .a_in(a_in[4]), .b_in(xor_5_out), .c_in(full_adder_4_c_out), .sum(sum[4]), .c_out(full_adder_5_c_out));
  xor xor_6 (xor_6_out, sub, b_in[5]);
  full_adder full_adder_6 (
    .a_in(a_in[5]), .b_in(xor_6_out), .c_in(full_adder_5_c_out), .sum(sum[5]), .c_out(full_adder_6_c_out));
  xor xor_7 (xor_7_out, sub, b_in[6]);
  full_adder full_adder_7 (
    .a_in(a_in[6]), .b_in(xor_7_out), .c_in(full_adder_6_c_out), .sum(sum[6]), .c_out(full_adder_7_c_out));
  xor xor_8 (xor_8_out, sub, b_in[7]);
  full_adder full_adder_8 (
    .a_in(a_in[7]), .b_in(xor_8_out), .c_in(full_adder_7_c_out), .sum(sum[7]), .c_out(full_adder_8_c_out));
  xor xor_9 (xor_9_out, sub, b_in[8]);
  full_adder full_adder_9 (
    .a_in(a_in[8]), .b_in(xor_9_out), .c_in(full_adder_8_c_out), .sum(sum[8]), .c_out(full_adder_9_c_out));
  xor xor_10 (xor_10_out, sub, b_in[9]);
  full_adder full_adder_10 (
    .a_in(a_in[9]), .b_in(xor_10_out), .c_in(full_adder_9_c_out), .sum(sum[9]), .c_out(full_adder_10_c_out));
  xor xor_11 (xor_11_out, sub, b_in[10]);
  full_adder full_adder_11 (
    .a_in(a_in[10]), .b_in(xor_11_out), .c_in(full_adder_10_c_out), .sum(sum[10]), .c_out(full_adder_11_c_out));
  xor xor_12 (xor_12_out, sub, b_in[11]);
  full_adder full_adder_12 (
    .a_in(a_in[11]), .b_in(xor_12_out), .c_in(full_adder_11_c_out), .sum(sum[11]), .c_out(full_adder_12_c_out));
  xor xor_13 (xor_13_out, sub, b_in[12]);
  full_adder full_adder_13 (
    .a_in(a_in[12]), .b_in(xor_13_out), .c_in(full_adder_12_c_out), .sum(sum[12]), .c_out(full_adder_13_c_out));
  xor xor_14 (xor_14_out, sub, b_in[13]);
  full_adder full_adder_14 (
    .a_in(a_in[13]), .b_in(xor_14_out), .c_in(full_adder_13_c_out), .sum(sum[13]), .c_out(full_adder_14_c_out));
  xor xor_15 (xor_15_out, sub, b_in[14]);
  full_adder full_adder_15 (
    .a_in(a_in[14]), .b_in(xor_15_out), .c_in(full_adder_14_c_out), .sum(sum[14]), .c_out(full_adder_15_c_out));
  xor xor_16 (xor_16_out, sub, b_in[15]);
  full_adder full_adder_16 (
    .a_in(a_in[15]), .b_in(xor_16_out), .c_in(full_adder_15_c_out), .sum(sum[15]), .c_out(full_adder_16_c_out));
  xor xor_17 (c_out, full_adder_16_c_out, full_adder_15_c_out);
endmodule

module ALU (
  input  [15:0] in1_val,
  input  [15:0] in2_val,
  input  [3:0] OpType,
  input  [2:0] shamt_in,
  output ovf,
  output [15:0] out_val,
  output bne,
  output ble
);

  wire add_ovf, less_than, not_2_out, sub_ovf;
  wire [15:0] add_val, In1_and_In2, left_shift, not_In1, right_shift, sub_val;

  check_gt check_gt_1 (.in_a(in1_val), .sub(1'b1), .in_b(in2_val), .sign_bit(less_than));  // open: diff, out_ovf
  sixteen_adder sixteen_adder_1 (.a_in(in1_val), .b_in(in2_val), .sum(add_val), .c_out(add_ovf));  // open: sub
  shifter_me_left shifter_me_left_1 (.in_a(in1_val), .sham_in(shamt_in), .shifted(left_shift));
  shifter_me_right shifter_me_right_1 (.in_a(in1_val), .sham_in(shamt_in), .shifted(right_shift));
  assign not_In1 = ~in1_val;  // NOT_Gate not_1, 16 bits wide
  assign In1_and_In2 = in1_val & in2_val;  // AND_Gate and_1, 16 bits wide
  Multiplexer #(.select(4), .width(16), .enable("false")) multiplexer_1 (
    .in0(add_val), .in1(add_val), .in2(sub_val), .in3(left_shift), .in4(right_shift), .in5(In1_and_In2),
    .in6(not_In1), .in7(add_val), .in8(add_val), .in13(add_val), .in14(add_val), .out(out_val), .sel(OpType));  // open: in9, in10, in11, in12, in15
  eq_check eq_check_1 (.val_a(in1_val), .val_b(in2_val), .bne_please_branch(bne));  // open: ble
  sixteen_adder sixteen_adder_2 (.a_in(in1_val), .sub(1'b1), .b_in(in2_val), .sum(sub_val), .c_out(sub_ovf));
  not not_2 (not_2_out, bne);
  or or_1 (ble, not_2_out, less_than);
  or or_2 (ovf, add_ovf, sub_ovf);

  // Other names for the same wires on the sheet: In1[15:0] = in1_val; In2[15:0] = in2_val; op_type[3:0] = OpType
endmodule

module shift_sub (
  input  [15:0] in_val,
  input  left_right
);

  wire and_1_out, and_2_out, and_3_out, and_4_out, not_1_out, s1_out;

  not not_1 (not_1_out, left_right);
  and and_1 (and_1_out, in_val[0], left_right);
  and and_2 (and_2_out, not_1_out, in_val[1]);
  or s1 (s1_out, and_1_out, and_4_out);
  and and_3 (and_3_out, in_val[1], left_right);
  and and_4 (and_4_out, not_1_out, in_val[2]);
  // OR_Gate s2 has open pins: in0=and_3_out, out=open
  // AND_Gate and_5 has open pins: in0=in_val[2], in1=left_right, out=open

  // Other names for the same wires on the sheet: in_0 = in_val[0]; in_1 = in_val[1]; in_2 = in_val[2];
  //   in_3 = in_val[3]; in_4 = in_val[4]; in_5 = in_val[5]; in_6 = in_val[6]; in_7 = in_val[7]; in_8 = in_val[8];
  //   in_9 = in_val[9]; in_10 = in_val[10]; in_11 = in_val[11]; in_12 = in_val[12]; in_13 = in_val[13];
  //   in_14 = in_val[14]; in_15 = in_val[15]
endmodule

module eq_check (
  input  [15:0] val_a,
  input  [15:0] val_b,
  output bne_please_branch,
  output ble
);

  wire and_1_out, and_2_out, and_3_out, and_4_out, and_5_out, and_6_out, and_7_out, and_8_out, and_9_out,
       and_10_out, and_11_out, and_12_out, and_13_out, and_14_out, and_15_out, and_16_out, eq, not_2_out,
       or_1_out, or_2_out, or_3_out, or_4_out, or_5_out, or_6_out, or_7_out, or_8_out, or_9_out, or_10_out,
       or_11_out, or_12_out, or_13_out, or_14_out, or_15_out, or_16_out, or_18_out;
  wire [15:0] xor_1_out;

  assign xor_1_out = val_b ^ val_a;  // XOR_Gate xor_1, 16 bits wide
  or or_1 (or_1_out, xor_1_out[0], 1'b0);
  or or_2 (or_2_out, xor_1_out[1], 1'b0);
  or or_3 (or_3_out, xor_1_out[2], 1'b0);
  or or_4 (or_4_out, xor_1_out[3], 1'b0);
  or or_5 (or_5_out, xor_1_out[4], 1'b0);
  or or_6 (or_6_out, xor_1_out[5], 1'b0);
  or or_7 (or_7_out, xor_1_out[6], 1'b0);
  or or_8 (or_8_out, xor_1_out[7], 1'b0);
  or or_9 (or_9_out, xor_1_out[8], 1'b0);
  or or_10 (or_10_out, xor_1_out[9], 1'b0);
  or or_11 (or_11_out, xor_1_out[10], 1'b0);
  or or_12 (or_12_out, xor_1_out[11], 1'b0);
  or or_13 (or_13_out, xor_1_out[12], 1'b0);
  or or_14 (or_14_out, xor_1_out[13], 1'b0);
  or or_15 (or_15_out, xor_1_out[14], 1'b0);
  or or_16 (or_16_out, xor_1_out[15], 1'b0);
  and and_1 (and_1_out, val_b[0], ~val_a[0]);  // AND_Gate
  and and_2 (and_2_out, val_b[1], ~val_a[1]);  // AND_Gate
  and and_3 (and_3_out, val_b[2], ~val_a[2]);  // AND_Gate
  and and_4 (and_4_out, val_b[3], ~val_a[3]);  // AND_Gate
  and and_5 (and_5_out, val_b[4], ~val_a[4]);  // AND_Gate
  and and_6 (and_6_out, val_b[5], ~val_a[5]);  // AND_Gate
  and and_7 (and_7_out, val_b[6], ~val_a[6]);  // AND_Gate
  and and_8 (and_8_out, val_b[7], ~val_a[7]);  // AND_Gate
  and and_9 (and_9_out, val_b[8], ~val_a[8]);  // AND_Gate
  and and_10 (and_10_out, val_b[9], ~val_a[9]);  // AND_Gate
  and and_11 (and_11_out, val_b[10], ~val_a[10]);  // AND_Gate
  and and_12 (and_12_out, val_b[11], ~val_a[11]);  // AND_Gate
  and and_13 (and_13_out, val_b[12], ~val_a[12]);  // AND_Gate
  and and_14 (and_14_out, val_b[13], ~val_a[13]);  // AND_Gate
  and and_15 (and_15_out, val_b[14], ~val_a[14]);  // AND_Gate
  and and_16 (and_16_out, val_b[15], ~val_a[15]);  // AND_Gate
  or or_17 (bne_please_branch, or_1_out, or_2_out, or_3_out, or_4_out, or_5_out, or_6_out, or_7_out, or_8_out, or_9_out, or_10_out, or_11_out, or_12_out, or_13_out, or_14_out, or_15_out, or_16_out);
  not not_1 (eq, bne_please_branch);
  or or_18 (or_18_out, and_1_out, and_2_out, and_3_out, and_4_out, and_5_out, and_6_out, and_7_out, and_8_out, and_9_out, and_10_out, and_11_out, and_12_out, and_13_out, and_14_out, and_15_out, and_16_out);
  not not_2 (not_2_out, or_18_out);
  or or_19 (ble, not_2_out, eq);

  // Other names for the same wires on the sheet: a_8 = val_b[8]; a_9 = val_b[9]; a_10 = val_b[10]; a_11 = val_b[11];
  //   a_12 = val_b[12]; a_13 = val_b[13]; a_14 = val_b[14]; a_15 = val_b[15]
endmodule

module check_gt (
  input  [15:0] in_a,
  input  sub,
  input  [15:0] in_b,
  output [15:0] diff,
  output sign_bit,
  output out_ovf
);

  wire full_adder_1_c_out, full_adder_2_c_out, full_adder_3_c_out, full_adder_4_c_out, full_adder_5_c_out,
       full_adder_6_c_out, full_adder_7_c_out, full_adder_8_c_out, full_adder_9_c_out, full_adder_10_c_out,
       full_adder_11_c_out, full_adder_12_c_out, full_adder_13_c_out, full_adder_14_c_out,
       full_adder_15_c_out, full_adder_16_c_out, xor_1_out, xor_2_out, xor_3_out, xor_4_out, xor_5_out,
       xor_6_out, xor_7_out, xor_8_out, xor_9_out, xor_10_out, xor_11_out, xor_12_out, xor_13_out,
       xor_14_out, xor_15_out, xor_16_out;

  xor xor_1 (xor_1_out, sub, in_b[0]);
  full_adder full_adder_1 (.a_in(in_a[0]), .b_in(xor_1_out), .c_in(sub), .sum(diff[0]), .c_out(full_adder_1_c_out));
  xor xor_2 (xor_2_out, sub, in_b[1]);
  full_adder full_adder_2 (
    .a_in(in_a[1]), .b_in(xor_2_out), .c_in(full_adder_1_c_out), .sum(diff[1]), .c_out(full_adder_2_c_out));
  xor xor_3 (xor_3_out, sub, in_b[2]);
  full_adder full_adder_3 (
    .a_in(in_a[2]), .b_in(xor_3_out), .c_in(full_adder_2_c_out), .sum(diff[2]), .c_out(full_adder_3_c_out));
  xor xor_4 (xor_4_out, sub, in_b[3]);
  full_adder full_adder_4 (
    .a_in(in_a[3]), .b_in(xor_4_out), .c_in(full_adder_3_c_out), .sum(diff[3]), .c_out(full_adder_4_c_out));
  xor xor_5 (xor_5_out, sub, in_b[4]);
  full_adder full_adder_5 (
    .a_in(in_a[4]), .b_in(xor_5_out), .c_in(full_adder_4_c_out), .sum(diff[4]), .c_out(full_adder_5_c_out));
  xor xor_6 (xor_6_out, sub, in_b[5]);
  full_adder full_adder_6 (
    .a_in(in_a[5]), .b_in(xor_6_out), .c_in(full_adder_5_c_out), .sum(diff[5]), .c_out(full_adder_6_c_out));
  xor xor_7 (xor_7_out, sub, in_b[6]);
  full_adder full_adder_7 (
    .a_in(in_a[6]), .b_in(xor_7_out), .c_in(full_adder_6_c_out), .sum(diff[6]), .c_out(full_adder_7_c_out));
  xor xor_8 (xor_8_out, sub, in_b[7]);
  full_adder full_adder_8 (
    .a_in(in_a[7]), .b_in(xor_8_out), .c_in(full_adder_7_c_out), .sum(diff[7]), .c_out(full_adder_8_c_out));
  xor xor_9 (xor_9_out, sub, in_b[8]);
  full_adder full_adder_9 (
    .a_in(in_a[8]), .b_in(xor_9_out), .c_in(full_adder_8_c_out), .sum(diff[8]), .c_out(full_adder_9_c_out));
  xor xor_10 (xor_10_out, sub, in_b[9]);
  full_adder full_adder_10 (
    .a_in(in_a[9]), .b_in(xor_10_out), .c_in(full_adder_9_c_out), .sum(diff[9]), .c_out(full_adder_10_c_out));
  xor xor_11 (xor_11_out, sub, in_b[10]);
  full_adder full_adder_11 (
    .a_in(in_a[10]), .b_in(xor_11_out), .c_in(full_adder_10_c_out), .sum(diff[10]),
    .c_out(full_adder_11_c_out));
  xor xor_12 (xor_12_out, sub, in_b[11]);
  full_adder full_adder_12 (
    .a_in(in_a[11]), .b_in(xor_12_out), .c_in(full_adder_11_c_out), .sum(diff[11]),
    .c_out(full_adder_12_c_out));
  xor xor_13 (xor_13_out, sub, in_b[12]);
  full_adder full_adder_13 (
    .a_in(in_a[12]), .b_in(xor_13_out), .c_in(full_adder_12_c_out), .sum(diff[12]),
    .c_out(full_adder_13_c_out));
  xor xor_14 (xor_14_out, sub, in_b[13]);
  full_adder full_adder_14 (
    .a_in(in_a[13]), .b_in(xor_14_out), .c_in(full_adder_13_c_out), .sum(diff[13]),
    .c_out(full_adder_14_c_out));
  xor xor_15 (xor_15_out, sub, in_b[14]);
  full_adder full_adder_15 (
    .a_in(in_a[14]), .b_in(xor_15_out), .c_in(full_adder_14_c_out), .sum(diff[14]),
    .c_out(full_adder_15_c_out));
  xor xor_16 (xor_16_out, sub, in_b[15]);
  full_adder full_adder_16 (
    .a_in(in_a[15]), .b_in(xor_16_out), .c_in(full_adder_15_c_out), .sum(diff[15]),
    .c_out(full_adder_16_c_out));
  xor xor_17 (out_ovf, full_adder_16_c_out, full_adder_15_c_out);

  assign sign_bit = diff[15];
endmodule

module shifter_me_left (
  input  [15:0] in_a,
  input  [2:0] sham_in,
  output [15:0] shifted
);

  wire multiplexer_1_out, multiplexer_2_out, multiplexer_3_out, multiplexer_4_out, multiplexer_5_out,
       multiplexer_6_out, multiplexer_7_out, multiplexer_8_out, multiplexer_9_out, multiplexer_10_out,
       multiplexer_11_out, multiplexer_12_out, multiplexer_13_out, multiplexer_14_out, multiplexer_15_out,
       multiplexer_16_out, multiplexer_17_out, multiplexer_18_out, multiplexer_19_out, multiplexer_20_out,
       multiplexer_21_out, multiplexer_22_out, multiplexer_23_out, multiplexer_24_out, multiplexer_25_out,
       multiplexer_26_out, multiplexer_27_out, multiplexer_28_out, multiplexer_29_out, multiplexer_30_out,
       multiplexer_31_out, multiplexer_32_out;

  Multiplexer #(.enable("false")) multiplexer_1 (
    .in0(in_a[15]), .in1(in_a[11]), .out(multiplexer_1_out), .sel(sham_in[2]));
  Multiplexer #(.enable("false")) multiplexer_2 (
    .in0(in_a[14]), .in1(in_a[10]), .out(multiplexer_2_out), .sel(sham_in[2]));
  Multiplexer #(.enable("false")) multiplexer_3 (
    .in0(in_a[13]), .in1(in_a[9]), .out(multiplexer_3_out), .sel(sham_in[2]));
  Multiplexer #(.enable("false")) multiplexer_4 (
    .in0(in_a[12]), .in1(in_a[8]), .out(multiplexer_4_out), .sel(sham_in[2]));
  Multiplexer #(.enable("false")) multiplexer_5 (
    .in0(in_a[11]), .in1(in_a[7]), .out(multiplexer_5_out), .sel(sham_in[2]));
  Multiplexer #(.enable("false")) multiplexer_6 (
    .in0(in_a[10]), .in1(in_a[6]), .out(multiplexer_6_out), .sel(sham_in[2]));
  Multiplexer #(.enable("false")) multiplexer_7 (
    .in0(in_a[9]), .in1(in_a[5]), .out(multiplexer_7_out), .sel(sham_in[2]));
  Multiplexer #(.enable("false")) multiplexer_8 (
    .in0(in_a[8]), .in1(in_a[4]), .out(multiplexer_8_out), .sel(sham_in[2]));
  Multiplexer #(.enable("false")) multiplexer_9 (
    .in0(in_a[7]), .in1(in_a[3]), .out(multiplexer_9_out), .sel(sham_in[2]));
  Multiplexer #(.enable("false")) multiplexer_10 (
    .in0(in_a[6]), .in1(in_a[2]), .out(multiplexer_10_out), .sel(sham_in[2]));
  Multiplexer #(.enable("false")) multiplexer_11 (
    .in0(in_a[5]), .in1(in_a[1]), .out(multiplexer_11_out), .sel(sham_in[2]));
  Multiplexer #(.enable("false")) multiplexer_12 (
    .in0(in_a[4]), .in1(in_a[0]), .out(multiplexer_12_out), .sel(sham_in[2]));
  Multiplexer #(.enable("false")) multiplexer_13 (
    .in0(in_a[3]), .in1(1'b0), .out(multiplexer_13_out), .sel(sham_in[2]));
  Multiplexer #(.enable("false")) multiplexer_14 (
    .in0(in_a[2]), .in1(1'b0), .out(multiplexer_14_out), .sel(sham_in[2]));
  Multiplexer #(.enable("false")) multiplexer_15 (
    .in0(in_a[1]), .in1(1'b0), .out(multiplexer_15_out), .sel(sham_in[2]));
  Multiplexer #(.enable("false")) multiplexer_16 (
    .in0(in_a[0]), .in1(1'b0), .out(multiplexer_16_out), .sel(sham_in[2]));
  Multiplexer #(.enable("false")) multiplexer_17 (
    .in0(multiplexer_1_out), .in1(multiplexer_3_out), .out(multiplexer_17_out), .sel(sham_in[1]));
  Multiplexer #(.enable("false")) multiplexer_18 (
    .in0(multiplexer_2_out), .in1(multiplexer_4_out), .out(multiplexer_18_out), .sel(sham_in[1]));
  Multiplexer #(.enable("false")) multiplexer_19 (
    .in0(multiplexer_3_out), .in1(multiplexer_5_out), .out(multiplexer_19_out), .sel(sham_in[1]));
  Multiplexer #(.enable("false")) multiplexer_20 (
    .in0(multiplexer_4_out), .in1(multiplexer_6_out), .out(multiplexer_20_out), .sel(sham_in[1]));
  Multiplexer #(.enable("false")) multiplexer_21 (
    .in0(multiplexer_5_out), .in1(multiplexer_7_out), .out(multiplexer_21_out), .sel(sham_in[1]));
  Multiplexer #(.enable("false")) multiplexer_22 (
    .in0(multiplexer_6_out), .in1(multiplexer_8_out), .out(multiplexer_22_out), .sel(sham_in[1]));
  Multiplexer #(.enable("false")) multiplexer_23 (
    .in0(multiplexer_7_out), .in1(multiplexer_9_out), .out(multiplexer_23_out), .sel(sham_in[1]));
  Multiplexer #(.enable("false")) multiplexer_24 (
    .in0(multiplexer_8_out), .in1(multiplexer_10_out), .out(multiplexer_24_out), .sel(sham_in[1]));
  Multiplexer #(.enable("false")) multiplexer_25 (
    .in0(multiplexer_9_out), .in1(multiplexer_11_out), .out(multiplexer_25_out), .sel(sham_in[1]));
  Multiplexer #(.enable("false")) multiplexer_26 (
    .in0(multiplexer_10_out), .in1(multiplexer_12_out), .out(multiplexer_26_out), .sel(sham_in[1]));
  Multiplexer #(.enable("false")) multiplexer_27 (
    .in0(multiplexer_11_out), .in1(multiplexer_13_out), .out(multiplexer_27_out), .sel(sham_in[1]));
  Multiplexer #(.enable("false")) multiplexer_28 (
    .in0(multiplexer_12_out), .in1(multiplexer_14_out), .out(multiplexer_28_out), .sel(sham_in[1]));
  Multiplexer #(.enable("false")) multiplexer_29 (
    .in0(multiplexer_13_out), .in1(multiplexer_15_out), .out(multiplexer_29_out), .sel(sham_in[1]));
  Multiplexer #(.enable("false")) multiplexer_30 (
    .in0(multiplexer_14_out), .in1(multiplexer_16_out), .out(multiplexer_30_out), .sel(sham_in[1]));
  Multiplexer #(.enable("false")) multiplexer_31 (
    .in0(multiplexer_15_out), .in1(1'b0), .out(multiplexer_31_out), .sel(sham_in[1]));
  Multiplexer #(.enable("false")) multiplexer_32 (
    .in0(multiplexer_16_out), .in1(1'b0), .out(multiplexer_32_out), .sel(sham_in[1]));
  Multiplexer #(.enable("false")) multiplexer_33 (
    .in0(multiplexer_17_out), .in1(multiplexer_18_out), .out(shifted[15]), .sel(sham_in[0]));
  Multiplexer #(.enable("false")) multiplexer_34 (
    .in0(multiplexer_18_out), .in1(multiplexer_19_out), .out(shifted[14]), .sel(sham_in[0]));
  Multiplexer #(.enable("false")) multiplexer_35 (
    .in0(multiplexer_19_out), .in1(multiplexer_20_out), .out(shifted[13]), .sel(sham_in[0]));
  Multiplexer #(.enable("false")) multiplexer_36 (
    .in0(multiplexer_20_out), .in1(multiplexer_21_out), .out(shifted[12]), .sel(sham_in[0]));
  Multiplexer #(.enable("false")) multiplexer_37 (
    .in0(multiplexer_21_out), .in1(multiplexer_22_out), .out(shifted[11]), .sel(sham_in[0]));
  Multiplexer #(.enable("false")) multiplexer_38 (
    .in0(multiplexer_22_out), .in1(multiplexer_23_out), .out(shifted[10]), .sel(sham_in[0]));
  Multiplexer #(.enable("false")) multiplexer_39 (
    .in0(multiplexer_23_out), .in1(multiplexer_24_out), .out(shifted[9]), .sel(sham_in[0]));
  Multiplexer #(.enable("false")) multiplexer_40 (
    .in0(multiplexer_24_out), .in1(multiplexer_25_out), .out(shifted[8]), .sel(sham_in[0]));
  Multiplexer #(.enable("false")) multiplexer_41 (
    .in0(multiplexer_25_out), .in1(multiplexer_26_out), .out(shifted[7]), .sel(sham_in[0]));
  Multiplexer #(.enable("false")) multiplexer_42 (
    .in0(multiplexer_26_out), .in1(multiplexer_27_out), .out(shifted[6]), .sel(sham_in[0]));
  Multiplexer #(.enable("false")) multiplexer_43 (
    .in0(multiplexer_27_out), .in1(multiplexer_28_out), .out(shifted[5]), .sel(sham_in[0]));
  Multiplexer #(.enable("false")) multiplexer_44 (
    .in0(multiplexer_28_out), .in1(multiplexer_29_out), .out(shifted[4]), .sel(sham_in[0]));
  Multiplexer #(.enable("false")) multiplexer_45 (
    .in0(multiplexer_29_out), .in1(multiplexer_30_out), .out(shifted[3]), .sel(sham_in[0]));
  Multiplexer #(.enable("false")) multiplexer_46 (
    .in0(multiplexer_30_out), .in1(multiplexer_31_out), .out(shifted[2]), .sel(sham_in[0]));
  Multiplexer #(.enable("false")) multiplexer_47 (
    .in0(multiplexer_31_out), .in1(multiplexer_32_out), .out(shifted[1]), .sel(sham_in[0]));
  Multiplexer #(.enable("false")) multiplexer_48 (
    .in0(multiplexer_32_out), .in1(1'b0), .out(shifted[0]), .sel(sham_in[0]));

  // Other names for the same wires on the sheet: r0 = in_a[0]; r1 = in_a[1]; r2 = in_a[2]; r3 = in_a[3]; r4 = in_a[4];
  //   r5 = in_a[5]; r6 = in_a[6]; r7 = in_a[7]; r8 = in_a[8]; r9 = in_a[9]; r10 = in_a[10]; r11 = in_a[11];
  //   r12 = in_a[12]; r13 = in_a[13]; r14 = in_a[14]; r15 = in_a[15]; s0 = sham_in[0]; s1 = sham_in[1];
  //   s2 = sham_in[2]; o0 = shifted[0]; o1 = shifted[1]; o2 = shifted[2]; o3 = shifted[3]; o4 = shifted[4];
  //   o5 = shifted[5]; o6 = shifted[6]; o7 = shifted[7]; o8 = shifted[8]; o9 = shifted[9]; o10 = shifted[10];
  //   o11 = shifted[11]; o12 = shifted[12]; o13 = shifted[13]; o14 = shifted[14]; o15 = shifted[15]
endmodule

module shifter_me_right (
  input  [15:0] in_a,
  input  [2:0] sham_in,
  output [15:0] shifted
);

  wire multiplexer_1_out, multiplexer_2_out, multiplexer_3_out, multiplexer_4_out, multiplexer_5_out,
       multiplexer_6_out, multiplexer_7_out, multiplexer_8_out, multiplexer_9_out, multiplexer_10_out,
       multiplexer_11_out, multiplexer_12_out, multiplexer_13_out, multiplexer_14_out, multiplexer_15_out,
       multiplexer_16_out, multiplexer_17_out, multiplexer_18_out, multiplexer_19_out, multiplexer_20_out,
       multiplexer_21_out, multiplexer_22_out, multiplexer_23_out, multiplexer_24_out, multiplexer_25_out,
       multiplexer_26_out, multiplexer_27_out, multiplexer_28_out, multiplexer_29_out, multiplexer_30_out,
       multiplexer_31_out, multiplexer_32_out;

  Multiplexer #(.enable("false")) multiplexer_1 (
    .in0(in_a[0]), .in1(in_a[4]), .out(multiplexer_1_out), .sel(sham_in[2]));
  Multiplexer #(.enable("false")) multiplexer_2 (
    .in0(in_a[1]), .in1(in_a[5]), .out(multiplexer_2_out), .sel(sham_in[2]));
  Multiplexer #(.enable("false")) multiplexer_3 (
    .in0(in_a[2]), .in1(in_a[6]), .out(multiplexer_3_out), .sel(sham_in[2]));
  Multiplexer #(.enable("false")) multiplexer_4 (
    .in0(in_a[3]), .in1(in_a[7]), .out(multiplexer_4_out), .sel(sham_in[2]));
  Multiplexer #(.enable("false")) multiplexer_5 (
    .in0(in_a[4]), .in1(in_a[8]), .out(multiplexer_5_out), .sel(sham_in[2]));
  Multiplexer #(.enable("false")) multiplexer_6 (
    .in0(in_a[5]), .in1(in_a[9]), .out(multiplexer_6_out), .sel(sham_in[2]));
  Multiplexer #(.enable("false")) multiplexer_7 (
    .in0(in_a[6]), .in1(in_a[10]), .out(multiplexer_7_out), .sel(sham_in[2]));
  Multiplexer #(.enable("false")) multiplexer_8 (
    .in0(in_a[7]), .in1(in_a[11]), .out(multiplexer_8_out), .sel(sham_in[2]));
  Multiplexer #(.enable("false")) multiplexer_9 (
    .in0(in_a[8]), .in1(in_a[12]), .out(multiplexer_9_out), .sel(sham_in[2]));
  Multiplexer #(.enable("false")) multiplexer_10 (
    .in0(in_a[9]), .in1(in_a[13]), .out(multiplexer_10_out), .sel(sham_in[2]));
  Multiplexer #(.enable("false")) multiplexer_11 (
    .in0(in_a[10]), .in1(in_a[14]), .out(multiplexer_11_out), .sel(sham_in[2]));
  Multiplexer #(.enable("false")) multiplexer_12 (
    .in0(in_a[11]), .in1(in_a[15]), .out(multiplexer_12_out), .sel(sham_in[2]));
  Multiplexer #(.enable("false")) multiplexer_13 (
    .in0(in_a[12]), .in1(1'b0), .out(multiplexer_13_out), .sel(sham_in[2]));
  Multiplexer #(.enable("false")) multiplexer_14 (
    .in0(in_a[13]), .in1(1'b0), .out(multiplexer_14_out), .sel(sham_in[2]));
  Multiplexer #(.enable("false")) multiplexer_15 (
    .in0(in_a[14]), .in1(1'b0), .out(multiplexer_15_out), .sel(sham_in[2]));
  Multiplexer #(.enable("false")) multiplexer_16 (
    .in0(in_a[15]), .in1(1'b0), .out(multiplexer_16_out), .sel(sham_in[2]));
  Multiplexer #(.enable("false")) multiplexer_17 (
    .in0(multiplexer_1_out), .in1(multiplexer_3_out), .out(multiplexer_17_out), .sel(sham_in[1]));
  Multiplexer #(.enable("false")) multiplexer_18 (
    .in0(multiplexer_2_out), .in1(multiplexer_4_out), .out(multiplexer_18_out), .sel(sham_in[1]));
  Multiplexer #(.enable("false")) multiplexer_19 (
    .in0(multiplexer_3_out), .in1(multiplexer_5_out), .out(multiplexer_19_out), .sel(sham_in[1]));
  Multiplexer #(.enable("false")) multiplexer_20 (
    .in0(multiplexer_4_out), .in1(multiplexer_6_out), .out(multiplexer_20_out), .sel(sham_in[1]));
  Multiplexer #(.enable("false")) multiplexer_21 (
    .in0(multiplexer_5_out), .in1(multiplexer_7_out), .out(multiplexer_21_out), .sel(sham_in[1]));
  Multiplexer #(.enable("false")) multiplexer_22 (
    .in0(multiplexer_6_out), .in1(multiplexer_8_out), .out(multiplexer_22_out), .sel(sham_in[1]));
  Multiplexer #(.enable("false")) multiplexer_23 (
    .in0(multiplexer_7_out), .in1(multiplexer_9_out), .out(multiplexer_23_out), .sel(sham_in[1]));
  Multiplexer #(.enable("false")) multiplexer_24 (
    .in0(multiplexer_8_out), .in1(multiplexer_10_out), .out(multiplexer_24_out), .sel(sham_in[1]));
  Multiplexer #(.enable("false")) multiplexer_25 (
    .in0(multiplexer_9_out), .in1(multiplexer_11_out), .out(multiplexer_25_out), .sel(sham_in[1]));
  Multiplexer #(.enable("false")) multiplexer_26 (
    .in0(multiplexer_10_out), .in1(multiplexer_12_out), .out(multiplexer_26_out), .sel(sham_in[1]));
  Multiplexer #(.enable("false")) multiplexer_27 (
    .in0(multiplexer_11_out), .in1(multiplexer_13_out), .out(multiplexer_27_out), .sel(sham_in[1]));
  Multiplexer #(.enable("false")) multiplexer_28 (
    .in0(multiplexer_12_out), .in1(multiplexer_14_out), .out(multiplexer_28_out), .sel(sham_in[1]));
  Multiplexer #(.enable("false")) multiplexer_29 (
    .in0(multiplexer_13_out), .in1(multiplexer_15_out), .out(multiplexer_29_out), .sel(sham_in[1]));
  Multiplexer #(.enable("false")) multiplexer_30 (
    .in0(multiplexer_14_out), .in1(multiplexer_16_out), .out(multiplexer_30_out), .sel(sham_in[1]));
  Multiplexer #(.enable("false")) multiplexer_31 (
    .in0(multiplexer_15_out), .in1(1'b0), .out(multiplexer_31_out), .sel(sham_in[1]));
  Multiplexer #(.enable("false")) multiplexer_32 (
    .in0(multiplexer_16_out), .in1(1'b0), .out(multiplexer_32_out), .sel(sham_in[1]));
  Multiplexer #(.enable("false")) multiplexer_33 (
    .in0(multiplexer_17_out), .in1(multiplexer_18_out), .out(shifted[0]), .sel(sham_in[0]));
  Multiplexer #(.enable("false")) multiplexer_34 (
    .in0(multiplexer_18_out), .in1(multiplexer_19_out), .out(shifted[1]), .sel(sham_in[0]));
  Multiplexer #(.enable("false")) multiplexer_35 (
    .in0(multiplexer_19_out), .in1(multiplexer_20_out), .out(shifted[2]), .sel(sham_in[0]));
  Multiplexer #(.enable("false")) multiplexer_36 (
    .in0(multiplexer_20_out), .in1(multiplexer_21_out), .out(shifted[3]), .sel(sham_in[0]));
  Multiplexer #(.enable("false")) multiplexer_37 (
    .in0(multiplexer_21_out), .in1(multiplexer_22_out), .out(shifted[4]), .sel(sham_in[0]));
  Multiplexer #(.enable("false")) multiplexer_38 (
    .in0(multiplexer_22_out), .in1(multiplexer_23_out), .out(shifted[5]), .sel(sham_in[0]));
  Multiplexer #(.enable("false")) multiplexer_39 (
    .in0(multiplexer_23_out), .in1(multiplexer_24_out), .out(shifted[6]), .sel(sham_in[0]));
  Multiplexer #(.enable("false")) multiplexer_40 (
    .in0(multiplexer_24_out), .in1(multiplexer_25_out), .out(shifted[7]), .sel(sham_in[0]));
  Multiplexer #(.enable("false")) multiplexer_41 (
    .in0(multiplexer_25_out), .in1(multiplexer_26_out), .out(shifted[8]), .sel(sham_in[0]));
  Multiplexer #(.enable("false")) multiplexer_42 (
    .in0(multiplexer_26_out), .in1(multiplexer_27_out), .out(shifted[9]), .sel(sham_in[0]));
  Multiplexer #(.enable("false")) multiplexer_43 (
    .in0(multiplexer_27_out), .in1(multiplexer_28_out), .out(shifted[10]), .sel(sham_in[0]));
  Multiplexer #(.enable("false")) multiplexer_44 (
    .in0(multiplexer_28_out), .in1(multiplexer_29_out), .out(shifted[11]), .sel(sham_in[0]));
  Multiplexer #(.enable("false")) multiplexer_45 (
    .in0(multiplexer_29_out), .in1(multiplexer_30_out), .out(shifted[12]), .sel(sham_in[0]));
  Multiplexer #(.enable("false")) multiplexer_46 (
    .in0(multiplexer_30_out), .in1(multiplexer_31_out), .out(shifted[13]), .sel(sham_in[0]));
  Multiplexer #(.enable("false")) multiplexer_47 (
    .in0(multiplexer_31_out), .in1(multiplexer_32_out), .out(shifted[14]), .sel(sham_in[0]));
  Multiplexer #(.enable("false")) multiplexer_48 (
    .in0(multiplexer_32_out), .in1(1'b0), .out(shifted[15]), .sel(sham_in[0]));

  // Other names for the same wires on the sheet: r0 = in_a[0]; r1 = in_a[1]; r2 = in_a[2]; r3 = in_a[3]; r4 = in_a[4];
  //   r5 = in_a[5]; r6 = in_a[6]; r7 = in_a[7]; r8 = in_a[8]; r9 = in_a[9]; r10 = in_a[10]; r11 = in_a[11];
  //   r12 = in_a[12]; r13 = in_a[13]; r14 = in_a[14]; r15 = in_a[15]; s0 = sham_in[0]; s1 = sham_in[1];
  //   s2 = sham_in[2]; o0 = shifted[0]; o1 = shifted[1]; o2 = shifted[2]; o3 = shifted[3]; o4 = shifted[4];
  //   o5 = shifted[5]; o6 = shifted[6]; o7 = shifted[7]; o8 = shifted[8]; o9 = shifted[9]; o10 = shifted[10];
  //   o11 = shifted[11]; o12 = shifted[12]; o13 = shifted[13]; o14 = shifted[14]; o15 = shifted[15]
endmodule
