// Logisim project vending.circ as structural Verilog: 1 circuit, main circuit main
module main (
  input  N,
  input  D,
  input  RESET,
  output DISPENSE,
  output DESPERATE,
  output DOH
);

  wire and_4_out, and_5_out, clock_1_out, DiQ2iQ0iN_out, iQ2iQ1iQ0NiD_out, iQ2iRESET1_out, iQ2iRESET_out,
       iQ2Q1_out, not_1_out, not_2_out, not_3_out, not_4_out, not_5_out, not_6_out, or_1_out, or_2_out, Q0,
       Q0iQ2iNiD_out, Q1, Q1iQ2iQ0_out, Q1NiQ0_out, Q1Q0D_out, Q2, Q2iNiD1_out, Q2iNiD_out, Q2iNiQ1_out,
       Q2ND_out, Q2Q1D_out, Q2Q1Q0_out, Q2Q1Q0iRESET_out;

  not not_1 (not_1_out, Q2);
  not not_2 (not_2_out, Q1);
  not not_3 (not_3_out, Q0);
  not not_4 (not_4_out, N);
  not not_5 (not_5_out, D);
  not not_6 (not_6_out, RESET);
  or Q2Q1Q0 (Q2Q1Q0_out, Q2, Q1, Q0);
  or Q2Q1D (Q2Q1D_out, Q2, Q1, D);
  or Q2ND (Q2ND_out, Q2, N, D);
  or iQ2iRESET (iQ2iRESET_out, not_1_out, not_6_out);
  or Q2iNiD (Q2iNiD_out, Q2, not_4_out, not_5_out);
  or Q1iQ2iQ0 (Q1iQ2iQ0_out, Q1, not_1_out, not_3_out);
  or iQ2Q1 (iQ2Q1_out, not_1_out, Q1);
  or Q1Q0D (Q1Q0D_out, Q2, Q0, D);
  or iQ2iRESET1 (iQ2iRESET1_out, not_1_out, not_6_out);
  or Q1NiQ0 (Q1NiQ0_out, Q1, N, not_3_out);
  or Q2iNiQ1 (Q2iNiQ1_out, Q2, not_2_out, not_4_out);
  or Q2iNiD1 (Q2iNiD1_out, Q2, not_4_out, not_5_out);
  and Q0iQ2iNiD (Q0iQ2iNiD_out, Q0, not_1_out, not_4_out, not_5_out);
  and DiQ2iQ0iN (DiQ2iQ0iN_out, D, not_1_out, not_3_out, not_4_out);
  and iQ2iQ1iQ0NiD (iQ2iQ1iQ0NiD_out, not_1_out, not_2_out, not_3_out, N, not_5_out);
  and Q2Q1Q0iRESET (Q2Q1Q0iRESET_out, Q2, Q1, Q0, not_6_out);
  or or_1 (or_1_out, not_3_out, Q1);
  Clock clock_1 (.out(clock_1_out));
  and and_1 (DISPENSE, or_1_out, Q2);
  and and_2 (DESPERATE, Q2, Q1);
  and and_3 (DOH, Q2, Q1, Q0);
  and and_4 (and_4_out, iQ2Q1_out, Q1Q0D_out, iQ2iRESET1_out, Q1NiQ0_out, Q2iNiQ1_out, Q2iNiD1_out);
  or or_2 (or_2_out, Q0iQ2iNiD_out, DiQ2iQ0iN_out, iQ2iQ1iQ0NiD_out, Q2Q1Q0iRESET_out);
  and and_5 (and_5_out, Q2Q1Q0_out, Q2Q1D_out, Q2ND_out, iQ2iRESET_out, Q2iNiD_out, Q1iQ2iQ0_out);
  D_Flip_Flop D2 (.D(and_5_out), .clk(clock_1_out), .Q(Q2));  // open: Qn, preset, reset
  D_Flip_Flop D1 (.D(and_4_out), .clk(clock_1_out), .Q(Q1));  // open: Qn, preset, reset
  D_Flip_Flop D0 (.D(or_2_out), .clk(clock_1_out), .Q(Q0));  // open: Qn, preset, reset
endmodule
